# Fritzing sketch fan-controller (saved by Fritzing 0.9.3b)
breadboards: 1

parts:
  U1 = NodeMCU V3.0
  DHT1 = DHT22 Humidity and Temperature Sensor
  F1 = Fan - Ventilador [package=THT]
  Q1 = MOSFET-NCHANNEL [package=to220v]
  R1 = Resistor [tolerance=±5% resistance=10k package="0805 [SMD]"]

nets:
  N1: U1.D1, Q1.G, R1.Pin_1
  N2: U1.D2, DHT1.DATA
  3V3: U1.3V3, DHT1.VDD
  N3: U1.GND#6, U1.GND#13, U1.GND#16, U1.GND#33, DHT1.GND, Q1.S
  VIN: U1.Vin, F1.5V, R1.Pin_0
  N4: F1.GND, Q1.D

custom parts:
  NodeMCU V3.0: ESP8266 based NodeMCU
  Fan - Ventilador: Ventilador de 2 pines, se encuentra comunmente en computadoras de escritorio
